# Fritzing sketch dog_scale (saved by Fritzing 0.9.4)
circuit board: 8.46667cm x 5.64444cm
breadboards: 1

parts:
  U1 = attiny85 [package=dip]
  Part1 = HX711 Weighing Sensor Module
  BAT1 = Battery Holders [package=battcon_12mm]
  LCM1602_IIC1 = LCM1602 IIC [part_number="LCM1602 IIC" chip_label="LCM1602 IIC" package="DIP (Dual Inline) [THT]"]
  J1 = Piezo Speaker

nets:
  N1: U1.Pin_2, Part1.DO/RX
  N2: U1.Pin_3, Part1.CK/TX
  N3: U1.Pin_4, Part1.GND, BAT1.-
  N4: U1.Pin_5, LCM1602_IIC1.SDA
  N5: U1.Pin_6, J1.pin2
  N6: U1.Pin_7, LCM1602_IIC1.SCL
  N7: U1.Pin_8, Part1.VCC, BAT1.+, J1.pin1
  N8: LCM1602_IIC1.LED_A, LCM1602_IIC1.LED_B

custom parts:
  LCM1602 IIC: I2C-Module to use a 1602 or 2004 LCD on with the wire.h libory Serial LCD Modul
